// Logisim project DES.circ as structural Verilog: 1 circuit, main circuit main
module main (
  input  in_1,
  input  in_2,
  input  [63:0] in_3
);

  wire Clock, clock_2_out, not_1_out;
  wire [31:0] L, R, undriven;
  wire [63:0] multiplexer_1_out;

  Clock clock_1 (.out(Clock));
  not not_1 (not_1_out, in_1);
  Multiplexer #(.width(64)) multiplexer_1 (
    .in0({in_3[6], in_3[14], in_3[22], in_3[30], in_3[38], in_3[46], in_3[54], in_3[62], in_3[4], in_3[12], in_3[20], in_3[28], in_3[36], in_3[44], in_3[52], in_3[60], in_3[2], in_3[10], in_3[18], in_3[26], in_3[34], in_3[42], in_3[50], in_3[56], in_3[0], in_3[8], in_3[16], in_3[24], in_3[32], in_3[40], in_3[48], in_3[57], in_3[7], in_3[15], in_3[23], in_3[31], in_3[39], in_3[47], in_3[55], in_3[63], in_3[5], in_3[13], in_3[21], in_3[29], in_3[37], in_3[45], in_3[53], in_3[61], in_3[3], in_3[11], in_3[19], in_3[27], in_3[35], in_3[43], in_3[51], in_3[59], in_3[1], in_3[9], in_3[17], in_3[25], in_3[33], in_3[41], in_3[49], in_3[58]}),
    .in1({R, undriven}), .out(multiplexer_1_out), .sel(not_1_out));
  Clock clock_2 (.out(clock_2_out));
  Register #(.trigger("high"), .width(64)) register_1 (
    .D(multiplexer_1_out), .en(1'b1), .clk(clock_2_out), .Q({L, R}), .clr(in_2));

  // Other names for the same wires on the sheet: IP[63:0] = {in_3[6], in_3[14], in_3[22], in_3[30], in_3[38], in_3[46], in_3[54], in_3[62], in_3[4], in_3[12], in_3[20], in_3[28], in_3[36], in_3[44], in_3[52], in_3[60], in_3[2], in_3[10], in_3[18], in_3[26], in_3[34], in_3[42], in_3[50], in_3[56], in_3[0], in_3[8], in_3[16], in_3[24], in_3[32], in_3[40], in_3[48], in_3[57], in_3[7], in_3[15], in_3[23], in_3[31], in_3[39], in_3[47], in_3[55], in_3[63], in_3[5], in_3[13], in_3[21], in_3[29], in_3[37], in_3[45], in_3[53], in_3[61], in_3[3], in_3[11], in_3[19], in_3[27], in_3[35], in_3[43], in_3[51], in_3[59], in_3[1], in_3[9], in_3[17], in_3[25], in_3[33], in_3[41], in_3[49], in_3[58]};
  //   IP58 = in_3[58]; IP50 = in_3[49]; IP42 = in_3[41]; IP34 = in_3[33]; IP26 = in_3[25]; IP18 = in_3[17];
  //   IP10 = in_3[9]; IP2 = in_3[1]; IP60 = in_3[59]; IP52 = in_3[51]; IP44 = in_3[43]; IP36 = in_3[35];
  //   IP28 = in_3[27]; IP20 = in_3[19]; IP12 = in_3[11]; IP4 = in_3[3]; IP62 = in_3[61]; IP54 = in_3[53];
  //   IP46 = in_3[45]; IP38 = in_3[37]; IP30 = in_3[29]; IP22 = in_3[21]; IP14 = in_3[13]; IP6 = in_3[5];
  //   IP64 = in_3[63]; IP56 = in_3[55]; IP48 = in_3[47]; IP40 = in_3[39]; IP32 = in_3[31]; IP24 = in_3[23];
  //   IP16 = in_3[15]; IP8 = in_3[7]; IP57 = in_3[57]; IP49 = in_3[48]; IP41 = in_3[40]; IP33 = in_3[32];
  //   IP25 = in_3[24]; IP17 = in_3[16]; IP9 = in_3[8]; IP1 = in_3[0]; IP59 = in_3[56]; IP51 = in_3[50];
  //   IP43 = in_3[42]; IP35 = in_3[34]; IP27 = in_3[26]; IP19 = in_3[18]; IP11 = in_3[10]; IP3 = in_3[2];
  //   IP61 = in_3[60]; IP53 = in_3[52]; IP45 = in_3[44]; IP37 = in_3[36]; IP29 = in_3[28]; IP21 = in_3[20];
  //   IP13 = in_3[12]; IP5 = in_3[4]; IP63 = in_3[62]; IP55 = in_3[54]; IP47 = in_3[46]; IP39 = in_3[38];
  //   IP31 = in_3[30]; IP23 = in_3[22]; IP15 = in_3[14]; IP7 = in_3[6]; Round[63:0] = {L, R}; Load_Data = in_1;
  //   Reset = in_2
endmodule
