// Logisim project key_schedule.circ as structural Verilog: 1 circuit, main circuit main
module main (
  input  in_1,
  input  in_2,
  input  [63:0] in_3
);

  wire Clock, clock_1_out, clock_2_out, clock_3_out, clock_5_out, clock_7_out, clock_9_out, Incr, not_1_out,
       not_2_out, not_3_out, Output_Enable, shift_register_1_p2, shift_register_3_p2, Shift_Schedule;
  wire [3:0] Shift_Counter_q;
  wire [27:0] C, CD;
  wire [55:0] CD1, CD2, multiplexer_1_out, multiplexer_2_out;

  LedBar #(.matrixcols(48)) ledbar_1 (
    .led0(C[3]), .led1(C[0]), .led2(C[7]), .led3(C[21]), .led4(C[13]), .led5(C[17]), .led6(C[24]),
    .led7(C[5]), .led8(C[27]), .led9(C[10]), .led10(C[20]), .led11(C[15]), .led12(C[19]), .led13(C[4]),
    .led14(C[16]), .led15(C[22]), .led16(C[11]), .led17(C[1]), .led18(C[26]), .led19(C[18]), .led20(C[8]),
    .led21(C[2]), .led22(C[23]), .led23(C[12]), .led24(CD[1]), .led25(CD[12]), .led26(CD[19]),
    .led27(CD[26]), .led28(CD[6]), .led29(CD[15]), .led30(CD[7]), .led31(CD[25]), .led32(CD[3]),
    .led33(CD[11]), .led34(CD[18]), .led35(CD[22]), .led36(CD[9]), .led37(CD[20]), .led38(CD[5]),
    .led39(CD[14]), .led40(CD[27]), .led41(CD[2]), .led42(CD[4]), .led43(CD[0]), .led44(CD[23]),
    .led45(CD[10]), .led46(CD[16]), .led47(CD[13]));
  Clock clock_1 (.out(clock_1_out));
  ROM #(.addrWidth(4), .dataWidth(1)) u_Shift_Schedule (.addr(Shift_Counter_q));  // open: data
  not not_1 (not_1_out, in_1);
  Counter #(.max('hf), .width(4)) Shift_Counter (
    .clr(in_2), .up(Incr), .count(Incr), .clk(clock_1_out), .Q(Shift_Counter_q));  // open: load, D, carry
  // Probe on {in_3[3], in_3[11], in_3[19], in_3[27], in_3[4], in_3[12], in_3[20], in_3[28], in_3[36], in_3[44], in_3[52], in_3[60], in_3[5], in_3[13], in_3[21], in_3[29], in_3[37], in_3[45], in_3[53], in_3[61], in_3[6], in_3[14], in_3[22], in_3[30], in_3[38], in_3[46], in_3[54], in_3[62], in_3[35], in_3[43], in_3[51], in_3[59], in_3[2], in_3[10], in_3[18], in_3[26], in_3[34], in_3[42], in_3[50], in_3[58], in_3[1], in_3[9], in_3[17], in_3[25], in_3[33], in_3[41], in_3[49], in_3[57], in_3[0], in_3[8], in_3[16], in_3[24], in_3[32], in_3[40], in_3[48], in_3[56]}
  not not_2 (not_2_out, in_1);
  Multiplexer #(.width(56)) multiplexer_1 (
    .in0({in_3[3], in_3[11], in_3[19], in_3[27], in_3[4], in_3[12], in_3[20], in_3[28], in_3[36], in_3[44], in_3[52], in_3[60], in_3[5], in_3[13], in_3[21], in_3[29], in_3[37], in_3[45], in_3[53], in_3[61], in_3[6], in_3[14], in_3[22], in_3[30], in_3[38], in_3[46], in_3[54], in_3[62], in_3[35], in_3[43], in_3[51], in_3[59], in_3[2], in_3[10], in_3[18], in_3[26], in_3[34], in_3[42], in_3[50], in_3[58], in_3[1], in_3[9], in_3[17], in_3[25], in_3[33], in_3[41], in_3[49], in_3[57], in_3[0], in_3[8], in_3[16], in_3[24], in_3[32], in_3[40], in_3[48], in_3[56]}),
    .in1(multiplexer_2_out), .out(multiplexer_1_out), .sel(not_2_out));
  Multiplexer #(.width(56)) multiplexer_2 (.in0(CD1), .in1(CD2), .out(multiplexer_2_out), .sel(Shift_Schedule));
  Clock clock_2 (.out(clock_2_out));
  Clock clock_3 (.out(clock_3_out));
  D_Flip_Flop d_ff_1 (.D(not_1_out), .clk(clock_2_out), .Q(Incr), .reset(in_2));  // open: Qn, preset
  Register #(.trigger("high"), .width(56)) register_1 (
    .D(multiplexer_1_out), .en(1'b1), .clk(clock_3_out), .Q({C, CD}), .clr(in_2));
  // Probe on Shift_Counter_q
  // Probe on {C, CD}
  Clock clock_4 (.out(Clock));
  not not_3 (not_3_out, in_1);
  Clock clock_5 (.out(clock_5_out));
  // Probe on in_3
  RAM #(.addrWidth(4), .dataWidth(48)) ram_1 (
    .addr(Shift_Counter_q), .we(not_3_out), .oe(Output_Enable), .clk(clock_5_out),
    .din({C[3], C[0], C[7], C[21], C[13], C[17], C[24], C[5], C[27], C[10], C[20], C[15], C[19], C[4], C[16], C[22], C[11], C[1], C[26], C[18], C[8], C[2], C[23], C[12], CD[1], CD[12], CD[19], CD[26], CD[6], CD[15], CD[7], CD[25], CD[3], CD[11], CD[18], CD[22], CD[9], CD[20], CD[5], CD[14], CD[27], CD[2], CD[4], CD[0], CD[23], CD[10], CD[16], CD[13]}));  // open: dout
  // Shift_Register #(.length(28)) shift_register_1: pin names not known; wires that end beside it: in_2, shift_register_1_p2, 1'b1, shift_register_1_p2, C[27]
  Clock clock_6 (.out(shift_register_1_p2));
  // Probe on CD1[55:28]
  Clock clock_7 (.out(clock_7_out));
  // Shift_Register #(.length(28)) shift_register_2: pin names not known; wires that end beside it: in_2, clock_7_out, 1'b1, clock_7_out, CD[27]
  // Probe on CD1[27:0]
  // Shift_Register #(.length(28)) shift_register_3: pin names not known; wires that end beside it: in_2, shift_register_3_p2, 1'b1, shift_register_3_p2, C[26], C[27]
  Clock clock_8 (.out(shift_register_3_p2));
  // Probe on CD2[55:28]
  Clock clock_9 (.out(clock_9_out));
  // Shift_Register #(.length(28)) shift_register_4: pin names not known; wires that end beside it: in_2, clock_9_out, 1'b1, clock_9_out, CD[26], CD[27]
  // Probe on CD2[27:0]

  // Other names for the same wires on the sheet: Init_Key[63:0] = in_3; PC56 = in_3[56]; PC48 = in_3[48];
  //   PC40 = in_3[40]; PC32 = in_3[32]; PC24 = in_3[24]; PC16 = in_3[16]; PC8 = in_3[8]; PC0 = in_3[0];
  //   PC57 = in_3[57]; PC49 = in_3[49]; PC41 = in_3[41]; PC33 = in_3[33]; PC25 = in_3[25]; PC17 = in_3[17];
  //   PC9 = in_3[9]; PC1 = in_3[1]; PC58 = in_3[58]; PC50 = in_3[50]; PC42 = in_3[42]; PC34 = in_3[34];
  //   PC26 = in_3[26]; PC18 = in_3[18]; PC10 = in_3[10]; PC2 = in_3[2]; PC59 = in_3[59]; PC51 = in_3[51];
  //   PC43 = in_3[43]; PC35 = in_3[35]; PC62 = in_3[62]; PC54 = in_3[54]; PC46 = in_3[46]; PC38 = in_3[38];
  //   PC30 = in_3[30]; PC22 = in_3[22]; PC14 = in_3[14]; PC6 = in_3[6]; PC61 = in_3[61]; PC53 = in_3[53];
  //   PC45 = in_3[45]; PC37 = in_3[37]; PC29 = in_3[29]; PC21 = in_3[21]; PC13 = in_3[13]; PC5 = in_3[5];
  //   PC60 = in_3[60]; PC52 = in_3[52]; PC44 = in_3[44]; PC36 = in_3[36]; PC28 = in_3[28]; PC20 = in_3[20];
  //   PC12 = in_3[12]; PC4 = in_3[4]; PC27 = in_3[27]; PC19 = in_3[19]; PC11 = in_3[11]; PC3 = in_3[3]; CD[55:28] = C;
  //   DS1[27:0] = CD1[27:0]; CS1[27:0] = CD1[55:28]; DS2[27:0] = CD2[27:0]; CS2[27:0] = CD2[55:28]; D[27:0] = CD;
  //   CD_13 = CD[13];
  //   K[47:0] = {C[3], C[0], C[7], C[21], C[13], C[17], C[24], C[5], C[27], C[10], C[20], C[15], C[19], C[4], C[16], C[22], C[11], C[1], C[26], C[18], C[8], C[2], C[23], C[12], CD[1], CD[12], CD[19], CD[26], CD[6], CD[15], CD[7], CD[25], CD[3], CD[11], CD[18], CD[22], CD[9], CD[20], CD[5], CD[14], CD[27], CD[2], CD[4], CD[0], CD[23], CD[10], CD[16], CD[13]};
  //   CD_16 = CD[16]; CD_10 = CD[10]; CD_23 = CD[23]; CD_0 = CD[0]; CD_4 = CD[4]; CD_2 = CD[2]; CD_27 = CD[27];
  //   CD_14 = CD[14]; CD_5 = CD[5]; CD_20 = CD[20]; CD_9 = CD[9]; CD_22 = CD[22]; CD_18 = CD[18]; CD_11 = CD[11];
  //   CD_3 = CD[3]; CD_25 = CD[25]; CD_7 = CD[7]; CD_15 = CD[15]; CD_6 = CD[6]; CD_26 = CD[26]; CD_19 = CD[19];
  //   CD_12 = CD[12]; CD_1 = CD[1]; CD_40 = C[12]; CD_51 = C[23]; CD_30 = C[2]; CD_36 = C[8]; CD_46 = C[18];
  //   CD_54 = C[26]; CD_29 = C[1]; CD_39 = C[11]; CD_50 = C[22]; CD_44 = C[16]; CD_32 = C[4]; CD_47 = C[19];
  //   CD_43 = C[15]; CD_48 = C[20]; CD_38 = C[10]; CD_55 = C[27]; CD_33 = C[5]; CD_52 = C[24]; CD_45 = C[17];
  //   CD_41 = C[13]; CD_49 = C[21]; CD_35 = C[7]; CD_28 = C[0]; CD_31 = C[3]; Load_Key = in_1; Reset = in_2

  // Notes on the sheet:
  //   contents of Shift_Schedule (hex, n*v repeats v):
  //   0 0 0 6*1 0 6*1
endmodule
